// Logisim project BANDA MATRIZ LED.circ as structural Verilog: 1 circuit, main circuit main
module main (
);

  wire button_1_out, clock_1_out, undriven, undriven_2, undriven_3, undriven_4, undriven_5;
  wire [16:0] counter_1_q, ram_1_data, shift_register_1_q0, shift_register_1_q1, shift_register_1_q2,
       shift_register_1_q3, shift_register_1_q4, shift_register_1_q5, shift_register_1_q6,
       shift_register_1_q7, shift_register_1_q8, shift_register_1_q9, shift_register_1_q10,
       shift_register_1_q11, shift_register_1_q12, shift_register_1_q13, shift_register_1_q14,
       shift_register_1_q15, shift_register_1_q16;

  // Buffer buffer_1 has open pins: in=undriven, out=open
  Button button_1 (.out(button_1_out));
  Clock clock_1 (.out(clock_1_out));
  Counter #(.width(17), .max('h1ffff)) counter_1 (
    .Q(counter_1_q), .clk(clock_1_out), .clr(button_1_out));  // open: load, D, count, carry
  // Buffer buffer_2 has open pins: in=undriven_2, out=open
  // Buffer buffer_3 has open pins: in=undriven_3, out=open
  DotMatrix #(.matrixcols(17), .matrixrows(17)) dotmatrix_1 (
    .col0(shift_register_1_q16), .col1(shift_register_1_q15), .col2(shift_register_1_q14),
    .col3(shift_register_1_q13), .col4(shift_register_1_q12), .col5(shift_register_1_q11),
    .col6(shift_register_1_q10), .col7(shift_register_1_q9), .col8(shift_register_1_q8),
    .col9(shift_register_1_q7), .col10(shift_register_1_q6), .col11(shift_register_1_q5),
    .col12(shift_register_1_q4), .col13(shift_register_1_q3), .col14(shift_register_1_q2),
    .col15(shift_register_1_q1), .col16(shift_register_1_q0));
  // Buffer buffer_4 has open pins: in=undriven_4, out=open
  RAM #(.addrWidth(17), .dataWidth(17)) ram_1 (
    .addr(counter_1_q), .data(ram_1_data), .clk(clock_1_out));  // open: sel, ld, clr
  Shift_Register #(.width(17), .length(17)) shift_register_1 (
    .in(ram_1_data), .clk(clock_1_out), .q0(shift_register_1_q0), .q1(shift_register_1_q1),
    .q2(shift_register_1_q2), .q3(shift_register_1_q3), .q4(shift_register_1_q4), .q5(shift_register_1_q5),
    .q6(shift_register_1_q6), .q7(shift_register_1_q7), .q8(shift_register_1_q8), .q9(shift_register_1_q9),
    .q10(shift_register_1_q10), .q11(shift_register_1_q11), .q12(shift_register_1_q12),
    .q13(shift_register_1_q13), .q14(shift_register_1_q14), .q15(shift_register_1_q15),
    .q16(shift_register_1_q16));  // open: shift, out, load, clr, d0, d1, d2, d3, d4, d5, d6, d7, d8, d9, d10, d11, d12, d13, d14, d15, d16
  // Buffer buffer_5 has open pins: in=undriven_5, out=open

  // Notes on the sheet:
  //   CONTADOR
  //   MATRIZ DE LED
  //   BOTÃO DE RESET MANUAL
  //   RAM
  //   REGISTRADOR DE  DESLOCAMENTO
endmodule
