// Logisim project CONTADOR ASSINCRONO 0-72.circ as structural Verilog: 2 circuits, main circuit DECODIFICADOR
module DECODIFICADOR (
  input  e1,
  input  e2,
  input  e3,
  input  e4,
  output a,
  output b,
  output c,
  output d,
  output e,
  output f,
  output g
);

  wire and_1_out, and_2_out, and_3_out, and_4_out, and_5_out, and_6_out, and_7_out, and_8_out, and_9_out,
       and_10_out, and_11_out, and_12_out, and_13_out, and_14_out, and_15_out, and_16_out, and_17_out,
       not_1_out, not_2_out, not_3_out, not_4_out, not_5_out, not_6_out, not_7_out, not_8_out, not_9_out,
       not_10_out, not_11_out, not_12_out, not_13_out, not_14_out, not_15_out, not_16_out, not_17_out,
       not_18_out, not_19_out, not_20_out, not_21_out;

  not not_1 (not_1_out, e2);
  and and_1 (and_1_out, not_1_out, not_2_out);
  not not_2 (not_2_out, e4);
  and and_2 (and_2_out, e2, e4);
  not not_3 (not_3_out, e2);
  not not_4 (not_4_out, e3);
  and and_3 (and_3_out, not_4_out, not_5_out);
  not not_5 (not_5_out, e4);
  and and_4 (and_4_out, e3, e4);
  not not_6 (not_6_out, e3);
  not not_7 (not_7_out, e2);
  and and_5 (and_5_out, not_7_out, not_8_out);
  not not_8 (not_8_out, e4);
  not not_9 (not_9_out, e2);
  and and_6 (and_6_out, not_9_out, e3);
  and and_7 (and_7_out, e3, not_10_out);
  not not_10 (not_10_out, e4);
  not not_11 (not_11_out, e3);
  and and_8 (and_8_out, e2, not_11_out, e4);
  not not_12 (not_12_out, e2);
  and and_9 (and_9_out, not_12_out, not_13_out);
  not not_13 (not_13_out, e4);
  and and_10 (and_10_out, e3, not_14_out);
  not not_14 (not_14_out, e4);
  and and_11 (and_11_out, e1, e2);
  not not_15 (not_15_out, e3);
  and and_12 (and_12_out, not_15_out, not_16_out);
  not not_16 (not_16_out, e4);
  and and_13 (and_13_out, e2, not_17_out);
  not not_17 (not_17_out, e3);
  and and_14 (and_14_out, e2, not_18_out);
  not not_18 (not_18_out, e4);
  not not_19 (not_19_out, e2);
  and and_15 (and_15_out, not_19_out, e3);
  and and_16 (and_16_out, e2, not_20_out);
  not not_20 (not_20_out, e3);
  and and_17 (and_17_out, e2, not_21_out);
  not not_21 (not_21_out, e4);
  or or_1 (a, and_1_out, e3, and_2_out, e1);
  or or_2 (b, not_3_out, and_3_out, and_4_out, e1);
  or or_3 (c, not_6_out, e4, e2, e1);
  or or_4 (d, and_5_out, and_6_out, and_7_out, and_8_out, e1);
  or or_5 (e, and_9_out, and_10_out, and_11_out);
  or or_6 (f, and_12_out, and_13_out, and_14_out, e1);
  or or_7 (g, and_15_out, and_16_out, and_17_out, e1);
endmodule

module main (
);

  wire _9, _72, A, A1, and_1_out, B, B1, C, C1, clock_1_out, D, D1, E, E1, F, F1, G, G1, or_1_out, Q0, Q1,
       Q2, Q3, Q4, Q5, Q6, Q7, t_ff_1_qn, t_ff_2_qn, t_ff_3_qn, t_ff_4_qn, t_ff_5_qn, t_ff_6_qn;

  Clock clock_1 (.out(clock_1_out));
  or or_1 (or_1_out, _9, _72);
  and and_1 (and_1_out, ~Q6, Q7);  // AND_Gate
  and and_2 (_72, Q0, Q1, Q4, Q5, Q6);
  T_Flip_Flop t_ff_1 (.clk(clock_1_out), .T(1'b1), .Q(Q0), .Qn(t_ff_1_qn), .reset(or_1_out));  // open: preset, en
  T_Flip_Flop t_ff_2 (.clk(or_1_out), .T(1'b1), .Q(Q4), .Qn(t_ff_2_qn), .reset(and_1_out));  // open: preset, en
  and and_3 (_9, Q1, Q3);
  T_Flip_Flop t_ff_3 (.clk(t_ff_1_qn), .T(1'b1), .Q(Q1), .Qn(t_ff_3_qn), .reset(or_1_out));  // open: preset, en
  T_Flip_Flop t_ff_4 (.clk(t_ff_2_qn), .T(1'b1), .Q(Q5), .Qn(t_ff_4_qn), .reset(and_1_out));  // open: preset, en
  T_Flip_Flop t_ff_5 (.clk(t_ff_3_qn), .T(1'b1), .Q(Q2), .Qn(t_ff_5_qn), .reset(or_1_out));  // open: preset, en
  T_Flip_Flop t_ff_6 (.clk(t_ff_4_qn), .T(1'b1), .Q(Q6), .Qn(t_ff_6_qn), .reset(and_1_out));  // open: preset, en
  _7_Segment_Display u_7_segment_display_1 (.g(G1), .f(F1), .a(A1), .b(B1), .e(E1), .d(D1), .c(C1));  // open: dp
  T_Flip_Flop t_ff_7 (.clk(t_ff_5_qn), .T(1'b1), .Q(Q3), .reset(or_1_out));  // open: Qn, preset, en
  T_Flip_Flop t_ff_8 (.clk(t_ff_6_qn), .T(1'b1), .Q(Q7), .reset(and_1_out));  // open: Qn, preset, en
  _7_Segment_Display u_7_segment_display_2 (.g(G), .f(F), .a(A), .b(B), .e(E), .d(D), .c(C));  // open: dp
  DECODIFICADOR decodificador_1 (.e1(Q3), .e2(Q2), .e3(Q1), .e4(Q0), .a(A), .b(B), .c(C), .d(D), .e(E), .f(F), .g(G));
  DECODIFICADOR decodificador_2 (
    .e1(Q7), .e2(Q6), .e3(Q5), .e4(Q4), .a(A1), .b(B1), .c(C1), .d(D1), .e(E1), .f(F1), .g(G1));
endmodule
