// Logisim project CONTADOR SINCRONO.circ as structural Verilog: 3 circuits, main circuit main
module main (
);

  wire A, A1, and_2_out, and_3_out, B, B1, C, C1, CLEAR, clock_1_out, D, D1, E, E1, F, F1, G, G1, L0, L1, L2,
       L3, M0, M1, M2, M3;

  Clock clock_1 (.out(clock_1_out));
  CONTADOR contador_1 (
    .CLOCK(clock_1_out), .ENTRADA(1'b1), .RESET(CLEAR), .out_4(L3), .out_5(L2), .out_6(L1), .out_7(L0));
  CONTADOR contador_2 (
    .CLOCK(clock_1_out), .ENTRADA(1'b1), .RESET(CLEAR), .out_4(M3), .out_5(M2), .out_6(M1), .out_7(M0));
  DECODIFICADOR decodificador_1 (.e1(L3), .e2(L2), .e3(L1), .e4(L0), .a(A), .b(B), .c(C), .d(D), .e(E), .f(F), .g(G));
  DECODIFICADOR decodificador_2 (
    .e1(M3), .e2(M2), .e3(M1), .e4(M0), .a(A1), .b(B1), .c(C1), .d(D1), .e(E1), .f(F1), .g(G1));
  _7_Segment_Display u_7_segment_display_1 (.g(G), .f(F), .a(A), .b(B), .e(E), .d(D), .c(C));  // open: dp
  and and_1 (CLEAR, and_2_out, and_3_out);
  and and_2 (and_2_out, ~L0, L1, ~L2, L3);  // AND_Gate
  and and_3 (and_3_out, ~M0, M1, ~M2, M3);  // AND_Gate
  _7_Segment_Display u_7_segment_display_2 (.g(G1), .f(F1), .a(A1), .b(B1), .e(E1), .d(D1), .c(C1));  // open: dp
endmodule

module CONTADOR (
  input  CLOCK,
  input  ENTRADA,
  input  RESET,
  output out_4,
  output out_5,
  output out_6,
  output out_7
);

  T_Flip_Flop #(.trigger("falling")) t_ff_1 (
    .clk(CLOCK), .T(ENTRADA), .Q(out_7), .reset(RESET));  // open: Qn, preset, en
  T_Flip_Flop #(.trigger("falling")) t_ff_2 (
    .clk(out_7), .T(ENTRADA), .Q(out_6), .reset(RESET));  // open: Qn, preset, en
  T_Flip_Flop #(.trigger("falling")) t_ff_3 (
    .clk(out_6), .T(ENTRADA), .Q(out_5), .reset(RESET));  // open: Qn, preset, en
  T_Flip_Flop #(.trigger("falling")) t_ff_4 (
    .clk(out_5), .T(ENTRADA), .Q(out_4), .reset(RESET));  // open: Qn, preset, en
endmodule

module DECODIFICADOR (
  input  e1,
  input  e2,
  input  e3,
  input  e4,
  output a,
  output b,
  output c,
  output d,
  output e,
  output f,
  output g
);

  wire and_1_out, and_2_out, and_3_out, and_4_out, and_5_out, and_6_out, and_7_out, and_8_out, and_9_out,
       and_10_out, and_11_out, and_12_out, and_13_out, and_14_out, and_15_out, and_16_out, and_17_out,
       not_1_out, not_2_out, not_3_out, not_4_out, not_5_out, not_6_out, not_7_out, not_8_out, not_9_out,
       not_10_out, not_11_out, not_12_out, not_13_out, not_14_out, not_15_out, not_16_out, not_17_out,
       not_18_out, not_19_out, not_20_out, not_21_out;

  not not_1 (not_1_out, e2);
  and and_1 (and_1_out, not_1_out, not_2_out);
  not not_2 (not_2_out, e4);
  and and_2 (and_2_out, e2, e4);
  not not_3 (not_3_out, e2);
  not not_4 (not_4_out, e3);
  and and_3 (and_3_out, not_4_out, not_5_out);
  not not_5 (not_5_out, e4);
  and and_4 (and_4_out, e3, e4);
  not not_6 (not_6_out, e3);
  not not_7 (not_7_out, e2);
  and and_5 (and_5_out, not_7_out, not_8_out);
  not not_8 (not_8_out, e4);
  not not_9 (not_9_out, e2);
  and and_6 (and_6_out, not_9_out, e3);
  and and_7 (and_7_out, e3, not_10_out);
  not not_10 (not_10_out, e4);
  not not_11 (not_11_out, e3);
  and and_8 (and_8_out, e2, not_11_out, e4);
  not not_12 (not_12_out, e2);
  and and_9 (and_9_out, not_12_out, not_13_out);
  not not_13 (not_13_out, e4);
  and and_10 (and_10_out, e3, not_14_out);
  not not_14 (not_14_out, e4);
  and and_11 (and_11_out, e1, e2);
  not not_15 (not_15_out, e3);
  and and_12 (and_12_out, not_15_out, not_16_out);
  not not_16 (not_16_out, e4);
  and and_13 (and_13_out, e2, not_17_out);
  not not_17 (not_17_out, e3);
  and and_14 (and_14_out, e2, not_18_out);
  not not_18 (not_18_out, e4);
  not not_19 (not_19_out, e2);
  and and_15 (and_15_out, not_19_out, e3);
  and and_16 (and_16_out, e2, not_20_out);
  not not_20 (not_20_out, e3);
  and and_17 (and_17_out, e2, not_21_out);
  not not_21 (not_21_out, e4);
  or or_1 (a, and_1_out, e3, and_2_out, e1);
  or or_2 (b, not_3_out, and_3_out, and_4_out, e1);
  or or_3 (c, not_6_out, e4, e2, e1);
  or or_4 (d, and_5_out, and_6_out, and_7_out, and_8_out, e1);
  or or_5 (e, and_9_out, and_10_out, and_11_out);
  or or_6 (f, and_12_out, and_13_out, and_14_out, e1);
  or or_7 (g, and_15_out, and_16_out, and_17_out, e1);
endmodule
