// Logisim project Coruja animação.circ as structural Verilog: 1 circuit, main circuit main
module main (
);

  wire clock_1_out;
  wire [31:0] multiplexer_1_out, multiplexer_2_out;

  Clock #(.highDuration(2), .lowDuration(6)) clock_1 (.out(clock_1_out));
  Multiplexer #(.width(32)) multiplexer_1 (
    .in0(32'hff00148), .in1(32'hff001c8), .out(multiplexer_1_out), .sel(clock_1_out));  // open: en
  Multiplexer #(.width(32)) multiplexer_2 (
    .in0(32'h7c00148), .in1(32'h7c001c8), .out(multiplexer_2_out), .sel(clock_1_out));  // open: en
  DotMatrix #(.matrixcols(32), .matrixrows(32)) dotmatrix_1 (
    .col0(32'hfe000000), .col1(32'hfe000000), .col2(32'hfe000000), .col3(32'h2000000), .col4(32'h2000000),
    .col5(32'h2000004), .col6(32'h200000c), .col7(32'h200000c), .col8(32'h2003ff8), .col9(32'he004018),
    .col10(32'h21f8008), .col11(32'hf100068), .col12(32'h3f001e8), .col13(multiplexer_1_out),
    .col14(32'h2c001c8), .col15(32'h2801c08), .col16(32'h28001c8), .col17(multiplexer_2_out),
    .col18(32'h2f001e8), .col19(32'h7f00068), .col20(32'h2900008), .col21(32'h71f8008), .col22(32'h2004018),
    .col23(32'h2003ff8), .col24(32'h200000c), .col25(32'h200000c), .col26(32'h2000000), .col27(32'h2000000),
    .col28(32'h2000000), .col29(32'h2000000), .col30(32'h2000000), .col31(32'h2000000));
endmodule
