// Logisim project Nave alien animação.circ as structural Verilog: 2 circuits, main circuit main
module main (
);

  wire clock_1_out, clock_2_out, clock_3_out;
  wire [5:0] random_1_out;
  wire [9:0] multiplexer_1_out, multiplexer_2_out, multiplexer_3_out, ram_1_data, shift_register_1_q0,
       shift_register_1_q1, shift_register_1_q2, shift_register_1_q3, shift_register_1_q4,
       shift_register_1_q5, shift_register_1_q6, shift_register_1_q7, shift_register_1_q8,
       shift_register_1_q9;

  Clock #(.highDuration(2), .lowDuration(6)) clock_1 (.out(clock_1_out));
  Clock clock_2 (.out(clock_2_out));
  Multiplexer #(.width(10)) multiplexer_1 (
    .in0(10'h58), .in1(10'h78), .out(multiplexer_1_out), .sel(clock_1_out));  // open: en
  Multiplexer #(.width(10)) multiplexer_2 (
    .in0(10'hdc), .in1(10'hfc), .out(multiplexer_2_out), .sel(clock_1_out));  // open: en
  Multiplexer #(.width(10)) multiplexer_3 (
    .in0(10'h58), .in1(10'h78), .out(multiplexer_3_out), .sel(clock_1_out));  // open: en
  Clock #(.highDuration(18), .lowDuration(18)) clock_3 (.out(clock_3_out));
  Random #(.width(6), .seed(1112)) random_1 (.clk(clock_2_out), .next(1'b1), .out(random_1_out));  // open: clr
  DotMatrix #(.matrixcols(10), .matrixrows(10)) dotmatrix_1 (
    .col0(10'h304), .col1(10'h310), .col2(10'h230), .col3(multiplexer_1_out), .col4(10'h27c),
    .col5(multiplexer_2_out), .col6(10'h7c), .col7(multiplexer_3_out), .col8(10'h131), .col9(10'h10));
  DotMatrix #(.matrixcols(10), .matrixrows(10), .persist(6)) dotmatrix_2 (
    .col0(shift_register_1_q9), .col1(shift_register_1_q8), .col2(shift_register_1_q7),
    .col3(shift_register_1_q6), .col4(shift_register_1_q5), .col5(shift_register_1_q4),
    .col6(shift_register_1_q3), .col7(shift_register_1_q2), .col8(shift_register_1_q1),
    .col9(shift_register_1_q0));
  RAM #(.addrWidth(6), .dataWidth(10)) ram_1 (
    .addr(random_1_out), .data(ram_1_data), .clk(clock_2_out));  // open: sel, ld, clr
  Shift_Register #(.width(10), .length(10)) shift_register_1 (
    .in(ram_1_data), .clk(clock_2_out), .clr(clock_3_out), .q0(shift_register_1_q0),
    .q1(shift_register_1_q1), .q2(shift_register_1_q2), .q3(shift_register_1_q3), .q4(shift_register_1_q4),
    .q5(shift_register_1_q5), .q6(shift_register_1_q6), .q7(shift_register_1_q7), .q8(shift_register_1_q8),
    .q9(shift_register_1_q9));  // open: shift, out, load, d0, d1, d2, d3, d4, d5, d6, d7, d8, d9
endmodule

module montanhas (
);

  wire clock_1_out;
  wire [5:0] random_1_out;
  wire [9:0] ram_1_data, shift_register_1_q0, shift_register_1_q1, shift_register_1_q2, shift_register_1_q3,
       shift_register_1_q4, shift_register_1_q5, shift_register_1_q6, shift_register_1_q7,
       shift_register_1_q8, shift_register_1_q9, shift_register_1_q10, shift_register_1_q11,
       shift_register_1_q12, shift_register_1_q13, shift_register_1_q14, shift_register_1_q15,
       shift_register_1_q16, shift_register_1_q17, shift_register_1_q18, shift_register_1_q19;

  Clock clock_1 (.out(clock_1_out));
  Random #(.width(6), .seed(1112)) random_1 (.clk(clock_1_out), .next(1'b1), .out(random_1_out));  // open: clr
  DotMatrix #(.matrixcols(20), .matrixrows(10), .persist(6)) dotmatrix_1 (
    .col0(shift_register_1_q19), .col1(shift_register_1_q18), .col2(shift_register_1_q17),
    .col3(shift_register_1_q16), .col4(shift_register_1_q15), .col5(shift_register_1_q14),
    .col6(shift_register_1_q13), .col7(shift_register_1_q12), .col8(shift_register_1_q11),
    .col9(shift_register_1_q10), .col10(shift_register_1_q9), .col11(shift_register_1_q8),
    .col12(shift_register_1_q7), .col13(shift_register_1_q6), .col14(shift_register_1_q5),
    .col15(shift_register_1_q4), .col16(shift_register_1_q3), .col17(shift_register_1_q2),
    .col18(shift_register_1_q1), .col19(shift_register_1_q0));
  RAM #(.addrWidth(6), .dataWidth(10)) ram_1 (
    .addr(random_1_out), .data(ram_1_data), .clk(clock_1_out));  // open: sel, ld, clr
  Shift_Register #(.width(10), .length(20)) shift_register_1 (
    .in(ram_1_data), .clk(clock_1_out), .q0(shift_register_1_q0), .q1(shift_register_1_q1),
    .q2(shift_register_1_q2), .q3(shift_register_1_q3), .q4(shift_register_1_q4), .q5(shift_register_1_q5),
    .q6(shift_register_1_q6), .q7(shift_register_1_q7), .q8(shift_register_1_q8), .q9(shift_register_1_q9),
    .q10(shift_register_1_q10), .q11(shift_register_1_q11), .q12(shift_register_1_q12),
    .q13(shift_register_1_q13), .q14(shift_register_1_q14), .q15(shift_register_1_q15),
    .q16(shift_register_1_q16), .q17(shift_register_1_q17), .q18(shift_register_1_q18),
    .q19(shift_register_1_q19));  // open: shift, out, load, clr, d0, d1, d2, d3, d4, d5, d6, d7, d8, d9, d10, d11, d12, d13, d14, d15, d16, d17, d18, d19
endmodule
