// Logisim project Nome vinicius matriz.circ as structural Verilog: 1 circuit, main circuit main
module main (
);

  wire clock_1_out;
  wire [5:0] counter_1_q;
  wire [8:0] ram_1_data, shift_register_1_q0, shift_register_1_q1, shift_register_1_q2, shift_register_1_q3,
       shift_register_1_q4, shift_register_1_q5, shift_register_1_q6, shift_register_1_q7,
       shift_register_1_q8;

  Clock clock_1 (.out(clock_1_out));
  Counter #(.width(6), .max('h3f), .ongoal("load")) counter_1 (
    .Q(counter_1_q), .clk(clock_1_out));  // open: load, D, count, carry, clr
  RAM #(.addrWidth(6), .dataWidth(9)) ram_1 (
    .addr(counter_1_q), .data(ram_1_data), .clk(clock_1_out));  // open: sel, ld, clr
  DotMatrix #(.matrixcols(9), .matrixrows(9)) dotmatrix_1 (
    .col0(shift_register_1_q8), .col1(shift_register_1_q7), .col2(shift_register_1_q6),
    .col3(shift_register_1_q5), .col4(shift_register_1_q4), .col5(shift_register_1_q3),
    .col6(shift_register_1_q2), .col7(shift_register_1_q1), .col8(shift_register_1_q0));
  Shift_Register #(.width(9), .length(9)) shift_register_1 (
    .in(ram_1_data), .clk(clock_1_out), .q0(shift_register_1_q0), .q1(shift_register_1_q1),
    .q2(shift_register_1_q2), .q3(shift_register_1_q3), .q4(shift_register_1_q4), .q5(shift_register_1_q5),
    .q6(shift_register_1_q6), .q7(shift_register_1_q7), .q8(shift_register_1_q8));  // open: shift, out, load, clr, d0, d1, d2, d3, d4, d5, d6, d7, d8
endmodule
