// Logisim project contador assincrono Vinicius 0-157.circ as structural Verilog: 2 circuits, main circuit main
module main (
);

  wire A, A1, A2, B, B1, B2, C, C1, C2, CLEAR_TOTAL, clock_1_out, D, D1, D2, DEZENA_5, DEZENA_9, E, E1, E2,
       F, F1, F2, G, G1, G2, Q0, Q1, Q2, Q3, Q4, Q5, Q6, Q7, Q8, Q9, Q10, Q11, STOP1, STOP2, t_ff_1_qn,
       t_ff_2_qn, t_ff_3_qn, t_ff_4_qn, t_ff_5_qn, t_ff_6_qn, t_ff_7_qn, t_ff_8_qn, t_ff_9_qn, UNIDADE_8,
       UNIDADE_9, UNIDADE_157;

  Clock clock_1 (.out(clock_1_out));
  T_Flip_Flop t_ff_1 (.clk(clock_1_out), .T(1'b1), .Q(Q0), .Qn(t_ff_1_qn), .reset(STOP1));  // open: preset, en
  T_Flip_Flop t_ff_2 (.clk(UNIDADE_9), .T(1'b1), .Q(Q4), .Qn(t_ff_2_qn), .reset(STOP2));  // open: preset, en
  T_Flip_Flop t_ff_3 (.clk(DEZENA_9), .T(1'b1), .Q(Q8), .Qn(t_ff_3_qn), .reset(CLEAR_TOTAL));  // open: preset, en
  T_Flip_Flop t_ff_4 (.clk(t_ff_1_qn), .T(1'b1), .Q(Q1), .Qn(t_ff_4_qn), .reset(STOP1));  // open: preset, en
  T_Flip_Flop t_ff_5 (.clk(t_ff_2_qn), .T(1'b1), .Q(Q5), .Qn(t_ff_5_qn), .reset(STOP2));  // open: preset, en
  T_Flip_Flop t_ff_6 (.clk(t_ff_3_qn), .T(1'b1), .Q(Q9), .Qn(t_ff_6_qn), .reset(CLEAR_TOTAL));  // open: preset, en
  and and_1 (CLEAR_TOTAL, UNIDADE_8, DEZENA_5, UNIDADE_157);
  or or_1 (STOP1, UNIDADE_9, CLEAR_TOTAL);
  T_Flip_Flop t_ff_7 (.clk(t_ff_4_qn), .T(1'b1), .Q(Q2), .Qn(t_ff_7_qn), .reset(STOP1));  // open: preset, en
  T_Flip_Flop t_ff_8 (.clk(t_ff_5_qn), .T(1'b1), .Q(Q6), .Qn(t_ff_8_qn), .reset(STOP2));  // open: preset, en
  T_Flip_Flop t_ff_9 (.clk(t_ff_6_qn), .T(1'b1), .Q(Q10), .Qn(t_ff_9_qn), .reset(CLEAR_TOTAL));  // open: preset, en
  T_Flip_Flop t_ff_10 (.clk(t_ff_7_qn), .T(1'b1), .Q(Q3), .reset(STOP1));  // open: Qn, preset, en
  T_Flip_Flop t_ff_11 (.clk(t_ff_8_qn), .T(1'b1), .Q(Q7), .reset(STOP2));  // open: Qn, preset, en
  T_Flip_Flop t_ff_12 (.clk(t_ff_9_qn), .T(1'b1), .Q(Q11), .reset(CLEAR_TOTAL));  // open: Qn, preset, en
  or or_2 (STOP2, DEZENA_9, CLEAR_TOTAL);
  Decodificador decodificador_1 (.e1(Q3), .e2(Q2), .e3(Q1), .e4(Q0), .a(A), .b(B), .c(C), .d(D), .e(E), .f(F), .g(G));
  _7_Segment_Display u_7_segment_display_1 (.g(G2), .f(F2), .a(A2), .b(B2), .e(E2), .d(D2), .c(C2));  // open: dp
  and and_2 (UNIDADE_9, Q3, Q1);
  and and_3 (DEZENA_9, Q5, Q7);
  and and_4 (UNIDADE_157, ~Q11, ~Q10, ~Q9, Q8);  // AND_Gate
  _7_Segment_Display u_7_segment_display_2 (.g(G1), .f(F1), .a(A1), .b(B1), .e(E1), .d(D1), .c(C1));  // open: dp
  Decodificador decodificador_2 (
    .e1(Q7), .e2(Q6), .e3(Q5), .e4(Q4), .a(A1), .b(B1), .c(C1), .d(D1), .e(E1), .f(F1), .g(G1));
  _7_Segment_Display u_7_segment_display_3 (.g(G), .f(F), .a(A), .b(B), .e(E), .d(D), .c(C));  // open: dp
  and and_5 (UNIDADE_8, ~Q0, ~Q1, ~Q2, Q3);  // AND_Gate
  and and_6 (DEZENA_5, Q4, Q6);
  Decodificador decodificador_3 (
    .e1(Q11), .e2(Q10), .e3(Q9), .e4(Q8), .a(A2), .b(B2), .c(C2), .d(D2), .e(E2), .f(F2), .g(G2));
endmodule

module Decodificador (
  input  e1,
  input  e2,
  input  e3,
  input  e4,
  output a,
  output b,
  output c,
  output d,
  output e,
  output f,
  output g
);

  wire and_1_out, and_2_out, and_3_out, and_4_out, and_5_out, and_6_out, and_7_out, and_8_out, and_9_out,
       and_10_out, and_11_out, and_12_out, and_13_out, and_14_out, and_15_out, and_16_out, and_17_out,
       not_1_out, not_2_out, not_3_out, not_4_out, not_5_out, not_6_out, not_7_out, not_8_out, not_9_out,
       not_10_out, not_11_out, not_12_out, not_13_out, not_14_out, not_15_out, not_16_out, not_17_out,
       not_18_out, not_19_out, not_20_out, not_21_out;

  not not_1 (not_1_out, e2);
  and and_1 (and_1_out, not_1_out, not_2_out);
  not not_2 (not_2_out, e4);
  and and_2 (and_2_out, e2, e4);
  not not_3 (not_3_out, e2);
  not not_4 (not_4_out, e3);
  and and_3 (and_3_out, not_4_out, not_5_out);
  not not_5 (not_5_out, e4);
  and and_4 (and_4_out, e3, e4);
  not not_6 (not_6_out, e3);
  not not_7 (not_7_out, e2);
  and and_5 (and_5_out, not_7_out, not_8_out);
  not not_8 (not_8_out, e4);
  not not_9 (not_9_out, e2);
  and and_6 (and_6_out, not_9_out, e3);
  and and_7 (and_7_out, e3, not_10_out);
  not not_10 (not_10_out, e4);
  and and_8 (and_8_out, e2, not_11_out, e4);
  not not_11 (not_11_out, e3);
  not not_12 (not_12_out, e2);
  and and_9 (and_9_out, not_12_out, not_13_out);
  not not_13 (not_13_out, e4);
  and and_10 (and_10_out, e3, not_14_out);
  not not_14 (not_14_out, e4);
  and and_11 (and_11_out, e1, e2);
  not not_15 (not_15_out, e3);
  and and_12 (and_12_out, not_15_out, not_16_out);
  not not_16 (not_16_out, e4);
  and and_13 (and_13_out, e2, not_17_out);
  not not_17 (not_17_out, e3);
  and and_14 (and_14_out, e2, not_18_out);
  not not_18 (not_18_out, e4);
  not not_19 (not_19_out, e2);
  and and_15 (and_15_out, not_19_out, e3);
  and and_16 (and_16_out, e2, not_20_out);
  not not_20 (not_20_out, e3);
  and and_17 (and_17_out, e2, not_21_out);
  not not_21 (not_21_out, e4);
  or or_1 (a, and_1_out, e3, and_2_out, e1);
  or or_2 (b, not_3_out, and_3_out, and_4_out, e1);
  or or_3 (c, not_6_out, e4, e2, e1);
  or or_4 (d, and_5_out, and_6_out, and_7_out, and_8_out, e1);
  or or_5 (e, and_9_out, and_10_out, and_11_out);
  or or_6 (f, and_12_out, and_13_out, and_14_out, e1);
  or or_7 (g, and_15_out, and_16_out, and_17_out, e1);
endmodule
