// Logisim project nome vini tty.circ as structural Verilog: 1 circuit, main circuit main
module main (
  input  in_1
);

  wire clock_4_out;
  wire [2:0] clock_3_out;
  wire [6:0] multiplexer_1_out;

  Multiplexer #(.select(3), .width(7)) multiplexer_1 (
    .in0(7'b1010110), .in1(7'b1001001), .in2(7'b1001110), .in3(7'b1001001), .in4(7'b1000011),
    .in5(7'b1001001), .in6(7'b1010101), .in7(7'b1010011), .out(multiplexer_1_out), .sel(clock_3_out));  // open: en
  Clock #(.highDuration(4), .lowDuration(4)) clock_1 (.out(clock_3_out[1]));
  Clock #(.highDuration(8), .lowDuration(8)) clock_2 (.out(clock_3_out[2]));
  Clock #(.highDuration(2), .lowDuration(2)) clock_3 (.out(clock_3_out[0]));
  TTY #(.cols(20)) tty_1 (.data(multiplexer_1_out), .clk(clock_4_out), .we(in_1));  // open: clr
  Clock clock_4 (.out(clock_4_out));
endmodule
