// Logisim project somador vini.circ as structural Verilog: 1 circuit, main circuit main
module main (
  input  [2:0] a,
  input  [2:0] a_2,
  input  [3:0] a_3,
  input  [3:0] a_4
);

  wire adder_1_cout, adder_2_cout, adder_4_cout, adder_5_cout, adder_6_cout, adder_7_cout;
  wire [3:0] adder_1_out, adder_4_out;

  Adder #(.width(1)) adder_1 (.a(a[0]), .b(a_2[0]), .out(adder_1_out[0]), .cin(1'b0), .cout(adder_1_cout));
  Adder #(.width(1)) adder_2 (.a(a[1]), .b(a_2[1]), .out(adder_1_out[1]), .cin(adder_1_cout), .cout(adder_2_cout));
  Adder #(.width(1)) adder_3 (.a(a[2]), .b(a_2[2]), .out(adder_1_out[2]), .cin(adder_2_cout), .cout(adder_1_out[3]));
  Adder #(.width(1)) adder_4 (.a(a_3[0]), .b(a_4[0]), .out(adder_4_out[0]), .cin(1'b0), .cout(adder_4_cout));
  Adder #(.width(1)) adder_5 (.a(a_3[1]), .b(a_4[1]), .out(adder_4_out[1]), .cin(adder_4_cout), .cout(adder_5_cout));
  Adder #(.width(1)) adder_6 (.a(a_3[2]), .b(a_4[2]), .out(adder_4_out[2]), .cin(adder_5_cout), .cout(adder_6_cout));
  Adder #(.width(1)) adder_7 (.a(a_3[3]), .b(a_4[3]), .out(adder_4_out[3]), .cin(adder_6_cout), .cout(adder_7_cout));
  Hex_Digit_Display hex_digit_display_1 (.value(adder_4_out));  // open: dp
  Hex_Digit_Display hex_digit_display_2 (.value(adder_1_out));  // open: dp
  // Probe on adder_1_out
  // Probe on adder_4_out
endmodule
